# Fritzing sketch arduino (saved by Fritzing 0.9.5d)
breadboards: 3

parts:
  元件1 = Arduino Uno (Rev3)
  DHT11 = Humidity and Temperature Sensor RHT03
  R1 = PHOTOCELL [package=photocell]
  10KΩ = Resistor [tolerance=±5% resistance=10000 package="1206 [SMD]"]
  YL-100 = Soil Moisture Sensor
  测距 = HC-SR04 Ultrasonic Distance Sensor
  MQ-9 = GAS_SENSOR [package=mq-3]
  1KΩ = Resistor [tolerance=±5% resistance=1000u package="1206 [SMD]"]  # not connected
  U1 = NodeMCU V1.0
  LED1 = smd LED [color="Red (633nm)" package="0603 [SMD]"]
  蜂鸣器 = Buzzer 12mm [package=buzzer-12mm-ns]
  IR1 = TSOP312.., 314.. [package=THT]
  LED4 = RGB LED (com. cathode, rgb) [package="5 mm [THT]"]
  J1 = Basic Servo
  LCD1 = LCD screen
  U2 = NodeMCU V1.0
  LED5 = smd LED [color="Red (633nm)" package="0603 [SMD]"]
  R2 = Rotary Potentiometer (Small) [maximum_resistance=100kΩ package=THT]

nets:
  N1: 元件1.A0, R1.P$2, 10KΩ.Pin_0
  N2: 元件1.A1, 元件1.D2, YL-100.DO, YL-100.AO
  N3: 元件1.A2, MQ-9.AO
  N4: 元件1.D10_PWM/SS, U1.D6
  N5: 元件1.D11_PWM/MOSI, U1.D5, U2.D7
  N6: 元件1.D3_PWM, DHT11.Data-signal
  N7: 元件1.D4, 测距.ECHO
  N8: 元件1.D5_PWM, 测距.TRIG
  N9: 元件1.D7, MQ-9.DO
  VCC: 元件1.5V, DHT11.Vcc, R1.P$1, YL-100.VCC, 测距.VCC, MQ-9.VCC
  GND: 元件1.GND, DHT11.GND_1, 10KΩ.Pin_1, YL-100.GND, 测距.GND, MQ-9.GND
  N10: U1.D0, LED1.anode
  N11: U1.D1, LED4.common_cathode
  N12: U1.D2, LED4.green_anode
  N13: U1.D3, LED4.blue_anode
  N14: U1.D4, 蜂鸣器.1
  3V3: U1.3V3, IR1.Vs, J1.vcc
  GND_2: U1.GND, LED1.cathode, 蜂鸣器.2, IR1.GND, LED4.red_anode, J1.gnd
  N15: U1.D7, IR1.Data
  VSS: LCD1.VSS, LCD1.R/W, LCD1.LED-, U2.GND, LED5.cathode, R2.leg2
  VDD: LCD1.VDD, LCD1.LED+, U2.3V3, R2.leg1
  N16: LCD1.V0, R2.wiper
  N17: LCD1.RS, U2.D0
  N18: LCD1.E, U2.D1
  N19: LCD1.DB4, U2.D2
  N20: LCD1.DB5, U2.D3
  N21: LCD1.DB6, U2.D4
  N22: LCD1.DB7, U2.D5
  N23: U2.D6, LED5.anode

custom parts:
  Soil Moisture Sensor: SparkFun Soil Moisture Sensor The SparkFun Soil Moisture Sensor is a simple breakout for measuring the moisture in soil and similar materials. The soil moisture sensor is pretty straight forward to use. The two large exposed pads function as probes for the sensor, together acting as a variable resistor. The more water that is in the soil means the better the conductivity between the pads will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
  GAS_SENSOR: MQ-3 alcohol gas sensor . FP not tested. SEN-08880.
  NodeMCU V1.0: ESP8266 based NodeMCU
