# Fritzing sketch 74HC138 (saved by Fritzing 0.9.5d)
breadboards: 1

parts:
  元件1 = Arduino Uno (Rev3) - ICSP
  LED1 = LED - 3mm [color="Red (633nm)" package="3 mm [THT]"]
  R3 = Resistor [tolerance=±5% resistance=220 package="1206 [SMD]"]
  LED2 = LED - 3mm [color="Red (633nm)" package="3 mm [THT]"]
  R4 = Resistor [tolerance=±5% resistance=220 package="1206 [SMD]"]
  LED3 = LED - 3mm [color="Red (633nm)" package="3 mm [THT]"]
  R5 = Resistor [tolerance=±5% resistance=220 package="1206 [SMD]"]
  LED4 = LED - 3mm [color="Red (633nm)" package="3 mm [THT]"]
  R6 = Resistor [tolerance=±5% resistance=220 package="1206 [SMD]"]
  LED5 = LED - 3mm [color="Red (633nm)" package="3 mm [THT]"]
  R7 = Resistor [tolerance=±5% resistance=220 package="1206 [SMD]"]
  LED6 = LED - 3mm [color="Red (633nm)" package="3 mm [THT]"]
  LED7 = LED - 3mm [color="Red (633nm)" package="3 mm [THT]"]
  LED8 = LED - 3mm [color="Red (633nm)" package="3 mm [THT]"]
  R8 = Resistor [tolerance=±5% resistance=220 package="1206 [SMD]"]
  R9 = Resistor [tolerance=±5% resistance=220 package="1206 [SMD]"]
  R10 = Resistor [tolerance=±5% resistance=220 package="1206 [SMD]"]
  74HC138 = 74HC139N [part_number=74HC139N package="DIP (Dual Inline) [THT]"]

nets:
  GND: 元件1.GND, 74HC138.1Y0, 74HC138.1Y1, 74HC138.GND
  N1: 元件1.D2, 74HC138.1G_
  N2: 元件1.D3_PWM, 74HC138.1A
  N3: 元件1.D4, 74HC138.1B
  3V3: 元件1.3V3, R3.Pin_0, R4.Pin_0, R5.Pin_0, R6.Pin_0, R7.Pin_0, R8.Pin_0, R9.Pin_0, R10.Pin_0, 74HC138.1Y2, 74HC138.VCC
  N4: LED1.cathode, 74HC138.2B
  N5: LED1.anode, R3.Pin_1
  N6: LED2.cathode, 74HC138.2G_
  N7: LED2.anode, R4.Pin_1
  N8: LED3.cathode, 74HC138.2A
  N9: LED3.anode, R5.Pin_1
  N10: LED4.cathode, 74HC138.2Y0
  N11: LED4.anode, R6.Pin_1
  N12: LED5.anode, R7.Pin_1
  N13: LED6.anode, R8.Pin_1
  N14: LED7.anode, R9.Pin_1
  N15: LED8.cathode, 74HC138.1Y3
  N16: LED8.anode, R10.Pin_1
